// Logisim project key.circ as structural Verilog: 1 circuit, main circuit main
module main (
  input  [7:0] in_1,
  input  [7:0] in_2,
  input  [7:0] in_3,
  input  in_4,
  input  [7:0] in_5,
  output [7:0] out_6,
  output [7:0] e,
  output [7:0] out_8,
  output [7:0] out_9
);

  wire button_1_out;
  wire [7:0] adder_1_out, multiplier_2_out, multiplier_3_out, subtractor_1_out, subtractor_2_out;

  Subtractor subtractor_1 (.a(in_1), .b(in_3), .out(subtractor_1_out));  // open: bin, bout
  Subtractor subtractor_2 (.a(in_2), .b(in_3), .out(subtractor_2_out));  // open: bin, bout
  Multiplier multiplier_1 (.a(in_1), .b(in_2), .out(out_6));  // open: cin, cout
  Multiplier multiplier_2 (.a(subtractor_1_out), .b(subtractor_2_out), .out(multiplier_2_out));  // open: cin, cout
  Counter #(.trigger("falling"), .behavior("old")) counter_1 (
    .Q(e), .clk(button_1_out), .clr(in_4));  // open: load, D, count, carry, preset
  Button button_1 (.out(button_1_out));
  Multiplier multiplier_3 (.a(multiplier_2_out), .b(in_5), .out(multiplier_3_out));  // open: cin, cout
  Adder adder_1 (.a(multiplier_3_out), .b(in_3), .out(adder_1_out));  // open: cin, cout
  Divider divider_1 (.a(multiplier_2_out), .b(e), .rem(out_8));  // open: out, upper
  Divider divider_2 (.a(adder_1_out), .b(e), .out(out_9));  // open: upper, rem

  // Notes on the sheet:
  //   P
  //   Q
  //   phi
  //   n
  //   d
endmodule
